# Fritzing sketch Design file (saved by Fritzing 0.9.3b)

parts:
  IC1 = L293D [package=THT]
  M1 = DC Motor
  Part2 = Bluetooth HC-05 Macho
  M2 = DC Motor
  R1 = Resistor [tolerance=±5% resistance=1k package="0805 [SMD]"]
  R2 = Resistor [tolerance=±5% resistance=2k package="0805 [SMD]"]
  Part3 = Arduino Nano (Rev3.0)
  U1 = LIPO-2000mAh [package=lipo-2000]
  TP1 = TP4056 [chip_label=TP4056 package="DIP (Dual Inline) [THT]"]
  M3 = 0.9v-5V booster usb output
  hc-sr1 = hc-sr04

nets:
  N1: IC1.Enable_1, Part3.D9
  N2: IC1.In_1, Part3.D2
  N3: IC1.Out_1_(_Controlled_by_Enable_1_), M1.pin_1
  GND: IC1.0V, R2.Pin_1, Part3.GND, TP1.pin6, M3.pin1, M3.pin4, hc-sr1.GND
  N4: IC1.Out_2_(_Controlled_by_Enable_1_), M1.pin_2
  N5: IC1.In_2, Part3.D3
  N6: IC1.+Vmotor, Part3.VIN, M3.pin3
  N7: IC1.Enable_2, Part3.D10
  N8: IC1.In_3, Part3.D5
  N9: IC1.Out_3_(_Controlled_by_Enable_2_), M2.pin_2
  N10: IC1.Out_4_(_Controlled_by_Enable_2_), M2.pin_1
  N11: IC1.In_4, Part3.D4
  N12: Part2.TXD, Part3.D0/RX
  N13: Part2.RXD, R1.Pin_1
  VCC: Part2.VCC, Part3.5V, hc-sr1.VCC
  N14: R1.Pin_0, Part3.D1/TX
  N15: Part3.D6, hc-sr1.Trig
  N16: Part3.D7, hc-sr1.Echo
  N17: U1.+, TP1.pin4
  N18: U1.-, TP1.pin5
  N19: TP1.pin3, M3.pin2

custom parts:
  TP4056: A DIP stand-in part for whatever IC you want. With 6 pins on a 300mil dual inline package (DIP) footprint.
  0.9v-5V booster usb output: 0.9 V ~ 5 V up 5 V DC - DC booster module.
