# Fritzing sketch Design File (saved by Fritzing 0.9.3b)

parts:
  Part1 = Arduino Nano (Rev3.0)
  J1 = Basic Servo
  e-radionica1 = TCS230 Color Sensor [part_number=101209]
  J2 = Infrared Proximity Sensor

nets:
  GND: Part1.GND, e-radionica1.Gnd, J2.GND
  N1: Part1.D2, e-radionica1.S0
  N2: Part1.D3, e-radionica1.S1
  N3: Part1.D4, e-radionica1.S2
  N4: Part1.D5, e-radionica1.S3
  N5: Part1.D6, e-radionica1.Out
  N6: Part1.D7, e-radionica1.OE
  N7: Part1.D11/MOSI, J1.pulse
  VCC: Part1.VIN, e-radionica1.Vcc, J2.Vcc
  N8: Part1.A0, J2.Vout

custom parts:
  TCS230 Color Sensor: TCS230
