# Fritzing sketch Design file (saved by Fritzing 0.9.3b)

parts:
  Part1 = Arduino Uno (Rev3) - ICSP
  IC1 = L293D [package=THT]
  M1 = DC Motor
  Part2 = Bluetooth HC-05 Macho
  VCC1 = 4 x AAA Battery Mount
  BAT1 = BC9VPC [package=bc9vpc]
  M2 = DC Motor
  R1 = Resistor [tolerance=±5% resistance=1k package="0805 [SMD]"]
  R2 = Resistor [tolerance=±5% resistance=2k package="0805 [SMD]"]

nets:
  N1: Part1.5V, IC1.Enable_2, IC1.+V
  N2: Part1.D0/RX, Part2.TXD
  N3: Part1.D1/TX, R1.Pin_0
  N4: Part1.D3_PWM, IC1.In_1
  N5: Part1.D4, IC1.In_2
  N6: Part1.D5_PWM, IC1.In_3
  N7: Part1.D6_PWM, IC1.In_4
  GND: Part1.GND, Part2.GND, BAT1.V-
  N8: Part1.VIN, BAT1.V+
  N9: IC1.Out_1_(_Controlled_by_Enable_1_), M1.pin_1
  N10: IC1.0V, VCC1.-, R2.Pin_1
  N11: IC1.Out_2_(_Controlled_by_Enable_1_), M1.pin_2
  N12: IC1.+Vmotor, VCC1.+
  N13: IC1.Out_3_(_Controlled_by_Enable_2_), M2.pin_2
  N14: IC1.Out_4_(_Controlled_by_Enable_2_), M2.pin_1
  N15: Part2.RXD, R1.Pin_1
