# Fritzing sketch Design File (saved by Fritzing 0.9.3b)

parts:
  Part1 = Arduino Nano (Rev3.0) (ICSP)
  Part2 = RFID-RC522-v2
  Tiny_RTC1 = Tiny RTC
  J1 = Piezo Speaker
  LED1 = smd LED [color="Red (633nm)" package="0805 [SMD]"]
  LED2 = smd LED [color="Red (633nm)" package="0805 [SMD]"]  # not connected
  LED3 = smd LED [color="Red (633nm)" package="0805 [SMD]"]  # not connected
  R1 = Resistor [tolerance=±5% resistance=220 package="0805 [SMD]"]
  R2 = Resistor [tolerance=±5% resistance=220 package="0805 [SMD]"]
  R3 = Resistor [tolerance=±5% resistance=220 package="0805 [SMD]"]

nets:
  GND: Part1.GND, Tiny_RTC1.GND, LED1.cathode
  N1: Part1.D2, R2.Pin_0
  N2: Part1.D3, R3.Pin_0
  N3: Part1.D4, R1.Pin_1
  N4: Part1.D6, J1.pin1
  N5: Part1.D9, Part2.SCK
  N6: Part1.D10, Part2.3.3V
  N7: Part1.D11/MOSI, Part2.GND
  N8: Part1.D12/MISO, Part2.IRQ
  5V: Part1.5V, Tiny_RTC1.VCC, J1.pin2
  N9: Part1.A5, Tiny_RTC1.SCL
  N10: Part1.A4, Tiny_RTC1.SDA
  N11: Part1.3V3, Part2.SDA
  N12: Part1.D13/SCK, Part2.RST

custom parts:
  RFID-RC522-v2: A simple China made RFID-RC522 Reader; do check the pin labels, as this is a MFRC522 based clone.
  Tiny RTC: Tiny RTC I2C module DS1370Z RTC and AT24C32 EEPROM
