# Fritzing sketch Design File (saved by Fritzing 0.9.3b)

parts:
  Part2 = RFID-RC522-v2
  WeMos_D1_Mini1 = WeMos D1 Mini
  Display1 = LCD screen 16x2 IIC [part_number=101290]

nets:
  N1: Part2.SDA, WeMos_D1_Mini1.D8
  N2: Part2.SCK, WeMos_D1_Mini1.D5
  N3: Part2.MOSI, WeMos_D1_Mini1.D7
  N4: Part2.MISO, WeMos_D1_Mini1.D6
  GND: Part2.GND, WeMos_D1_Mini1.G, Display1.GND
  N5: Part2.RST, WeMos_D1_Mini1.D0
  3.3V: Part2.3.3V, WeMos_D1_Mini1.3V3
  5V: WeMos_D1_Mini1.5V, Display1.VCC
  N6: WeMos_D1_Mini1.D1, Display1.SCL
  N7: WeMos_D1_Mini1.D2, Display1.SDA

custom parts:
  RFID-RC522-v2: A simple China made RFID-RC522 Reader; do check the pin labels, as this is a MFRC522 based clone.
  LCD screen 16x2 IIC: LCD screen with HD44780 controller enables showing text, symbols, value or anything else that comes from Croduino/Arduino. It is capable of showing 16 symbols in two lines and therefore can be used in many projects that need to send clearly visible and legible output information.. • Color of symbols: White • Backlight: Blue • Dimensions: 80 x 36 x 12 mm • Screen dimensions: 64.5 x 16 mm •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
